// Digital circuit 16-bit-comparator.dig as structural Verilog
module _16_bit_comparator (
  input  [15:0] a,
  input  [15:0] b,
  output eq
);

  wire _8_bit_comparator_1_eq, _8_bit_comparator_2_eq;

  _8_bit_comparator _8_bit_comparator_1 (.a(a[7:0]), .b(b[7:0]), .eq(_8_bit_comparator_1_eq));
  _8_bit_comparator _8_bit_comparator_2 (.a(a[15:8]), .b(b[15:8]), .eq(_8_bit_comparator_2_eq));
  and and_1 (eq, _8_bit_comparator_1_eq, _8_bit_comparator_2_eq);
endmodule
