// Digital circuit 2-bit-comparator.dig as structural Verilog
module _2_bit_comparator (
  input  [1:0] a,
  input  [1:0] b,
  output eq
);

  wire _1_bit_comparator_1_eq, _1_bit_comparator_2_eq;

  _1_bit_comparator _1_bit_comparator_1 (.a(a[0]), .b(b[0]), .eq(_1_bit_comparator_1_eq));
  _1_bit_comparator _1_bit_comparator_2 (.a(a[1]), .b(b[1]), .eq(_1_bit_comparator_2_eq));
  and and_1 (eq, _1_bit_comparator_1_eq, _1_bit_comparator_2_eq);
endmodule
