// Digital circuit 2reasonswhy.dig as structural Verilog
module _2reasonswhy (
  input  [6:0] opcode,
  input  [2:0] funct3,
  input  [6:0] funct7,
  output RFW,
  output [1:0] PCsel,
  output [1:0] WDsel,
  output [2:0] ALUSrcB,
  output [2:0] ALUOP,
  output ALUSrcA,
  output [4:0] INUM,
  output [1:0] BRAOP,
  output MLD,
  output MST,
  output [1:0] MZD
);

  wire add_2_eq, add_eq, addi_eq, and_1_out, and_2_out, and_3_out, and_4_out, and_5_out, and_6_out,
       and_7_out, and_8_out, and_9_out, and_10_out, and_11_out, and_12_out, and_13_out, and_14_out,
       and_15_out, and_16_out, and_17_out, and_18_out, and_19_out, and_20_out, and_21_out, and_22_out,
       ANDR_2_eq, ANDR_eq, BEQ_eq, BGE_eq, BLT_eq, BNE_eq, i_type_2_eq, i_type_3_eq, i_type_eq,
       i_type_jar_eq, j_type_eq, jal_r_eq, LB_eq, LD_eq, LW_eq, mul_2_eq, mul_eq, OR_2_eq, OR_3_eq, OR_eq,
       r_type_2_eq, r_type_3_eq, r_type_4_eq, r_type_5_eq, r_type_6_eq, r_type_7_eq, r_type_8_eq,
       r_type_9_eq, r_type_10_eq, r_type_11_eq, r_type_12_eq, r_type_13_eq, r_type_14_eq, r_type_15_eq,
       r_type_16_eq, r_type_17_eq, r_type_18_eq, r_type_eq, SB_eq, SD_eq, SLL_2_eq, SLL_eq, SLLI_eq,
       SRL_2_eq, SRL_eq, SRLA_eq, SRLI_eq, sub_2_eq, sub_eq, SW_eq;

  // Probe on funct7
  Comparator #(.Bits(7)) i_type (.a(opcode), .b(7'b0010011), .eq(i_type_eq));  // open: gt, lt
  Comparator #(.Bits(3)) addi (.a(funct3), .b(3'b000), .eq(addi_eq));  // open: gt, lt
  Comparator #(.Bits(7)) r_type (.a(opcode), .b(7'b0110011), .eq(r_type_eq));  // open: gt, lt
  Comparator #(.Bits(3)) add (.a(funct3), .b(3'b000), .eq(add_eq));  // open: gt, lt
  Comparator #(.Bits(7)) add_2 (.a(funct7), .b({7{1'b0}}), .eq(add_2_eq));  // open: gt, lt
  Comparator #(.Bits(7)) j_type (.a(opcode), .b(7'b1101111), .eq(j_type_eq));  // open: gt, lt
  Comparator #(.Bits(7)) i_type_jar (.a(opcode), .b(7'b1100111), .eq(i_type_jar_eq));  // open: gt, lt
  Comparator #(.Bits(3)) jal_r (.a(funct3), .b(3'b000), .eq(jal_r_eq));  // open: gt, lt
  Comparator #(.Bits(7)) r_type_2 (.a(opcode), .b(7'b0110011), .eq(r_type_2_eq));  // open: gt, lt
  Comparator #(.Bits(3)) sub (.a(funct3), .b(3'b000), .eq(sub_eq));  // open: gt, lt
  // Probe on funct7
  Comparator #(.Bits(7)) sub_2 (.a(funct7), .b(7'b0100000), .eq(sub_2_eq));  // open: gt, lt
  Comparator #(.Bits(7)) r_type_3 (.a(opcode), .b(7'b0110011), .eq(r_type_3_eq));  // open: gt, lt
  Comparator #(.Bits(3)) mul (.a(funct3), .b(3'b000), .eq(mul_eq));  // open: gt, lt
  // Probe on funct7
  Comparator #(.Bits(7)) mul_2 (.a(funct7), .b(7'b0000001), .eq(mul_2_eq));  // open: gt, lt
  Comparator #(.Bits(7)) r_type_4 (.a(opcode), .b(7'b0110011), .eq(r_type_4_eq));  // open: gt, lt
  Comparator #(.Bits(3)) SLL (.a(funct3), .b(3'b001), .eq(SLL_eq));  // open: gt, lt
  Comparator #(.Bits(7)) SLL_2 (.a(funct7), .b({7{1'b0}}), .eq(SLL_2_eq));  // open: gt, lt
  and and_1 (and_1_out, i_type_eq, addi_eq);
  and and_2 (and_2_out, r_type_eq, add_eq, add_2_eq);
  and and_3 (and_3_out, i_type_jar_eq, jal_r_eq);
  and and_4 (and_4_out, r_type_2_eq, sub_eq, sub_2_eq);
  and and_5 (and_5_out, r_type_3_eq, mul_eq, mul_2_eq);
  and and_6 (and_6_out, r_type_4_eq, SLL_eq, SLL_2_eq);
  and and_7 (and_7_out, i_type_2_eq, SRLI_eq);
  and and_8 (and_8_out, r_type_5_eq, SRL_2_eq, SRL_eq);
  and and_9 (and_9_out, i_type_3_eq, SLLI_eq);
  Comparator #(.Bits(3)) SRLI (.a(funct3), .b(3'b101), .eq(SRLI_eq));  // open: gt, lt
  Comparator #(.Bits(7)) i_type_2 (.a(opcode), .b(7'b0010011), .eq(i_type_2_eq));  // open: gt, lt
  Comparator #(.Bits(7)) SRL (.a(funct7), .b({7{1'b0}}), .eq(SRL_eq));  // open: gt, lt
  Comparator #(.Bits(3)) SRL_2 (.a(funct3), .b(3'b101), .eq(SRL_2_eq));  // open: gt, lt
  Comparator #(.Bits(7)) r_type_5 (.a(opcode), .b(7'b0110011), .eq(r_type_5_eq));  // open: gt, lt
  Comparator #(.Bits(3)) SLLI (.a(funct3), .b(3'b001), .eq(SLLI_eq));  // open: gt, lt
  Comparator #(.Bits(7)) i_type_3 (.a(opcode), .b(7'b0010011), .eq(i_type_3_eq));  // open: gt, lt
  // Probe on funct7
  // Probe on funct7
  // Probe on funct7
  Comparator #(.Bits(7)) r_type_6 (.a(opcode), .b(7'b1100011), .eq(r_type_6_eq));  // open: gt, lt
  Comparator #(.Bits(3)) BEQ (.a(funct3), .b(3'b000), .eq(BEQ_eq));  // open: gt, lt
  Comparator #(.Bits(7)) r_type_7 (.a(opcode), .b(7'b1100011), .eq(r_type_7_eq));  // open: gt, lt
  Comparator #(.Bits(3)) BLT (.a(funct3), .b(3'b100), .eq(BLT_eq));  // open: gt, lt
  Comparator #(.Bits(7)) r_type_8 (.a(opcode), .b(7'b1100011), .eq(r_type_8_eq));  // open: gt, lt
  Comparator #(.Bits(3)) BGE (.a(funct3), .b(3'b101), .eq(BGE_eq));  // open: gt, lt
  Comparator #(.Bits(7)) r_type_9 (.a(opcode), .b(7'b1100011), .eq(r_type_9_eq));  // open: gt, lt
  Comparator #(.Bits(3)) BNE (.a(funct3), .b(3'b001), .eq(BNE_eq));  // open: gt, lt
  Comparator #(.Bits(7)) r_type_10 (.a(opcode), .b(7'b0000011), .eq(r_type_10_eq));  // open: gt, lt
  Comparator #(.Bits(3)) LD (.a(funct3), .b(3'b011), .eq(LD_eq));  // open: gt, lt
  Comparator #(.Bits(7)) r_type_11 (.a(opcode), .b(7'b0100011), .eq(r_type_11_eq));  // open: gt, lt
  Comparator #(.Bits(3)) SD (.a(funct3), .b(3'b011), .eq(SD_eq));  // open: gt, lt
  Comparator #(.Bits(7)) r_type_12 (.a(opcode), .b(7'b0000011), .eq(r_type_12_eq));  // open: gt, lt
  Comparator #(.Bits(3)) LW (.a(funct3), .b(3'b010), .eq(LW_eq));  // open: gt, lt
  Comparator #(.Bits(7)) r_type_13 (.a(opcode), .b(7'b0100011), .eq(r_type_13_eq));  // open: gt, lt
  Comparator #(.Bits(3)) SW (.a(funct3), .b(3'b010), .eq(SW_eq));  // open: gt, lt
  Comparator #(.Bits(7)) r_type_14 (.a(opcode), .b(7'b0000011), .eq(r_type_14_eq));  // open: gt, lt
  Comparator #(.Bits(3)) LB (.a(funct3), .b(3'b000), .eq(LB_eq));  // open: gt, lt
  Comparator #(.Bits(7)) r_type_15 (.a(opcode), .b(7'b0100011), .eq(r_type_15_eq));  // open: gt, lt
  Comparator #(.Bits(3)) SB (.a(funct3), .b(3'b000), .eq(SB_eq));  // open: gt, lt
  Comparator #(.Bits(7)) r_type_16 (.a(opcode), .b(7'b0110011), .eq(r_type_16_eq));  // open: gt, lt
  Comparator #(.Bits(3)) OR (.a(funct3), .b(3'b110), .eq(OR_eq));  // open: gt, lt
  Comparator #(.Bits(7)) OR_2 (.a(funct7), .b({7{1'b0}}), .eq(OR_2_eq));  // open: gt, lt
  Comparator #(.Bits(7)) r_type_17 (.a(opcode), .b(7'b0110011), .eq(r_type_17_eq));  // open: gt, lt
  Comparator #(.Bits(3)) ANDR (.a(funct3), .b(3'b111), .eq(ANDR_eq));  // open: gt, lt
  Comparator #(.Bits(7)) ANDR_2 (.a(funct7), .b({7{1'b0}}), .eq(ANDR_2_eq));  // open: gt, lt
  Comparator #(.Bits(7)) r_type_18 (.a(opcode), .b(7'b0110011), .eq(r_type_18_eq));  // open: gt, lt
  Comparator #(.Bits(3)) SRLA (.a(funct3), .b(3'b101), .eq(SRLA_eq));  // open: gt, lt
  Comparator #(.Bits(7)) OR_3 (.a(funct7), .b(7'b0100000), .eq(OR_3_eq));  // open: gt, lt
  and and_10 (and_10_out, r_type_6_eq, BEQ_eq);
  and and_11 (and_11_out, r_type_7_eq, BLT_eq);
  and and_12 (and_12_out, r_type_8_eq, BGE_eq);
  and and_13 (and_13_out, r_type_9_eq, BNE_eq);
  and and_14 (and_14_out, r_type_10_eq, LD_eq);
  and and_15 (and_15_out, r_type_11_eq, SD_eq);
  and and_16 (and_16_out, r_type_12_eq, LW_eq);
  and and_17 (and_17_out, r_type_13_eq, SW_eq);
  and and_18 (and_18_out, r_type_14_eq, LB_eq);
  and and_19 (and_19_out, r_type_15_eq, SB_eq);
  and and_20 (and_20_out, r_type_16_eq, OR_eq, OR_2_eq);
  and and_21 (and_21_out, r_type_17_eq, ANDR_eq, ANDR_2_eq);
  and and_22 (and_22_out, r_type_18_eq, SRLA_eq, OR_3_eq);
  PriorityEncoder #(.Selector_Bits(5)) u_INUM (
    .in0(and_1_out), .in1(and_2_out), .in2(j_type_eq), .in3(and_3_out), .in4(and_4_out), .in5(and_5_out),
    .in6(and_6_out), .in7(and_9_out), .in8(and_8_out), .in9(and_7_out), .in10(and_10_out), .in11(and_11_out),
    .in12(and_12_out), .in13(and_13_out), .in14(and_14_out), .in15(and_15_out), .in16(and_16_out),
    .in17(and_17_out), .in18(and_18_out), .in19(and_19_out), .in20(and_20_out), .in21(and_21_out),
    .in22(and_22_out), .in23(1'b0), .in24(1'b0), .in25(1'b0), .in26(1'b0), .in27(1'b0), .in28(1'b0),
    .in29(1'b0), .in30(1'b0), .in31(1'b0), .num(INUM));  // open: any
  // Probe on INUM
  ROM #(.AddrBits(5), .Bits(18)) rom_1 (
    .A(INUM), .sel(1'b1), .D({MZD, MLD, MST, RFW, ALUOP, ALUSrcA, ALUSrcB, PCsel, WDsel, BRAOP}));
  // Probe on {MZD, MLD, MST, RFW, ALUOP, ALUSrcA, ALUSrcB, PCsel, WDsel, BRAOP}
  // Probe on RFW
  // Probe on ALUOP
  // Probe on ALUSrcA
  // Probe on ALUSrcB
  // Probe on PCsel
  // Probe on WDsel
  // Probe on BRAOP

  // Notes on the sheet:
  //   contents of rom_1 (hex, n*v repeats v):
  //   2040,2000,2294,2054,2400,2c00,3000,3140,3800,3940,2e4,2e6,2e7
  //   ,2e5,a048,c108,1a048,1c108,2a048,2c108,2800,3400,3c00
endmodule

/* Test case addi:
opcode  funct3  funct7  BRAOP  WDsel  PCsel  ALUSrcA  ALUSrcB  ALUOP  RFW  MST
0010011 000     000     00      00     00     0        001      000    1     0
*/

/* Test case sub:
opcode funct3 funct7 BRAOP WDsel PCsel ALUSrcA ALUSrcB ALUOP RFW MST
0b0110011 0b000 0b0100000 0b00 0b00 0b00 0b0 0b000 0b001 0b1 0b0
*/

/* Test case SRL:
opcode funct3 funct7 BRAOP WDsel PCsel ALUSrcA ALUSrcB ALUOP RFW MST
0b0110011 0b101 0b0000000 0b00 0b00 0b00 0b0 0b000 0b110 0b1 0b0
*/

/* Test case BGE:
opcode funct3 funct7 BRAOP WDsel PCsel ALUSrcA ALUSrcB ALUOP RFW MST
0b1100011 0b101 0b0000000 0b11 0b01 0b10 0b1 0b011 0b000 0b0 0b0
*/

/* Test case LW:
opcode funct3 funct7 MZD MLD MST RFW ALUOP ALUSrcA ALUSrcB PCsel WDsel BRAOP
0b0000011 0b010 0b0000000 0b01 0b1 0b0 0b1 0b000 0b0 0b001 0b00 0b10 0b00
*/

/* Test case OR:
opcode funct3 funct7 BRAOP WDsel PCsel ALUSrcA ALUSrcB ALUOP RFW MST
0b0110011 0b110 0b0000000 0b00 0b00 0b00 0b0 0b000 0b010 0b1 0b0
*/

/* Test case add:
opcode  funct3  funct7  BRAOP  WDsel  PCsel  ALUSrcA  ALUSrcB  ALUOP  RFW  MST
0b0110011 000     0000000 00      00     00     0        000      000    1     0
*/

/* Test case MUL:
opcode funct3 funct7 BRAOP WDsel PCsel ALUSrcA ALUSrcB ALUOP RFW MST
0b0110011 0b000 0b0000001 0b00 0b00 0b00 0b0 0b000 0b011 0b1 0b0
*/

/* Test case SRLI:
opcode funct3 funct7 BRAOP WDsel PCsel ALUSrcA ALUSrcB ALUOP RFW MST
0b0010011 0b101 0b0000000 0b00 0b00 0b00 0b0 0b101 0b110 0b1 0b0
*/

/* Test case BNE:
opcode funct3 funct7 MZD MLD MST RFW ALUOP ALUSrcA ALUSrcB PCsel WDsel BRAOP
0b1100011 0b001 0b0000000 0b00 0b0 0b0 0b0 0b000 0b1 0b011 0b10 0b01 0b01
*/

/* Test case SW:
opcode funct3 funct7 MZD MLD MST RFW ALUOP ALUSrcA ALUSrcB PCsel WDsel BRAOP
0b0100011 0b010 0b0000000 0b01 0b1 0b1 0b0 0b000 0b0 0b100 0b00 0b10 0b00
*/

/* Test case AND:
opcode funct3 funct7 BRAOP WDsel PCsel ALUSrcA ALUSrcB ALUOP RFW MST
0b0110011 0b111 0b0000000 0b00 0b00 0b00 0b0 0b000 0b101 0b1 0b0
*/

/* Test case jal:
opcode funct3 funct7 BRAOP WDsel PCsel ALUSrcA ALUSrcB ALUOP RFW MST
0b1101111 0b000 0b0000000 0b00 0b01 0b01 0b1 0b010 0b000 0b1 0b0
*/

/* Test case SLL:
opcode funct3 funct7 BRAOP WDsel PCsel ALUSrcA ALUSrcB ALUOP RFW MST
0b0110011 0b001 0b0000000 0b00 0b00 0b00 0b0 0b000 0b100 0b1 0b0
*/

/* Test case BEQ:
opcode funct3 funct7 BRAOP WDsel PCsel ALUSrcA ALUSrcB ALUOP RFW MST
0b1100011 0b000 0b0000000 0b00 0b01 0b10 0b1 0b011 0b000 0b0 0b0
*/

/* Test case LD:
opcode funct3 funct7 MZD MLD MST RFW ALUOP ALUSrcA ALUSrcB PCsel WDsel BRAOP
0b0000011 0b011 0b0000000 0b00 0b1 0b0 0b1 0b000 0b0 0b001 0b00 0b10 0b00
*/

/* Test case LB:
opcode funct3 funct7 MZD MLD MST RFW ALUOP ALUSrcA ALUSrcB PCsel WDsel BRAOP
0b0000011 0b000 0b0000000 0b10 0b1 0b0 0b1 0b000 0b0 0b001 0b00 0b10 0b00
*/

/* Test case SRLA:
opcode funct3 funct7 BRAOP WDsel PCsel ALUSrcA ALUSrcB ALUOP RFW MST  
0b0110011 0b101 0b00100000 0b00 0b00 0b00 0b0 0b000 0b111 0b1 0b0
*/

/* Test case jalr:
opcode funct3 funct7 BRAOP WDsel PCsel ALUSrcA ALUSrcB ALUOP RFW MST
0b1100111 0b000 0b0000000 0b00 0b01 0b01 0b0 0b001 0b000 0b1 0b0
*/

/* Test case SLLI:
opcode funct3 funct7 BRAOP WDsel PCsel ALUSrcA ALUSrcB ALUOP RFW MST
0b0010011 0b001 0b0000000 0b00 0b00 0b00 0b0 0b101 0b100 0b1 0b0
*/

/* Test case BLT:
opcode funct3 funct7 BRAOP WDsel PCsel ALUSrcA ALUSrcB ALUOP RFW MST
0b1100011 0b100 0b0000000 0b10 0b01 0b10 0b1 0b011 0b000 0b0 0b0
*/

/* Test case SD:
opcode funct3 funct7 MZD MLD MST RFW ALUOP ALUSrcA ALUSrcB PCsel WDsel BRAOP
0b0100011 0b011 0b0000000 0b00 0b1 0b1 0b0 0b000 0b0 0b100 0b00 0b10 0b00
*/

/* Test case SB:
opcode funct3 funct7 MZD MLD MST RFW ALUOP ALUSrcA ALUSrcB PCsel WDsel BRAOP
0b0100011 0b000 0b0000000 0b10 0b1 0b1 0b0 0b000 0b0 0b100 0b00 0b10 0b00
*/
