// Digital circuit 32-bit-comparator.dig as structural Verilog
module _32_bit_comparator (
  input  [31:0] a,
  input  [31:0] b,
  output eq
);

  wire _16_bit_comparator_1_eq, _16_bit_comparator_2_eq;

  _16_bit_comparator _16_bit_comparator_1 (.a(a[15:0]), .b(b[15:0]), .eq(_16_bit_comparator_1_eq));
  _16_bit_comparator _16_bit_comparator_2 (.a(a[31:16]), .b(b[31:16]), .eq(_16_bit_comparator_2_eq));
  and and_1 (eq, _16_bit_comparator_1_eq, _16_bit_comparator_2_eq);
endmodule
