// Digital circuit 4-bit-comparator.dig as structural Verilog
module _4_bit_comparator (
  input  [3:0] a,
  input  [3:0] b,
  output eq
);

  wire _2_bit_comparator_1_eq, _2_bit_comparator_2_eq;

  _2_bit_comparator _2_bit_comparator_1 (.a(a[1:0]), .b(b[1:0]), .eq(_2_bit_comparator_1_eq));
  _2_bit_comparator _2_bit_comparator_2 (.a(a[3:2]), .b(b[3:2]), .eq(_2_bit_comparator_2_eq));
  and and_1 (eq, _2_bit_comparator_1_eq, _2_bit_comparator_2_eq);
endmodule
