// Digital circuit 8-bit-comparator.dig as structural Verilog
module _8_bit_comparator (
  input  [7:0] a,
  input  [7:0] b,
  output eq
);

  wire _4_bit_comparator_1_eq, _4_bit_comparator_2_eq;

  _4_bit_comparator _4_bit_comparator_1 (.a(a[3:0]), .b(b[3:0]), .eq(_4_bit_comparator_1_eq));
  _4_bit_comparator _4_bit_comparator_2 (.a(a[7:4]), .b(b[7:4]), .eq(_4_bit_comparator_2_eq));
  and and_1 (eq, _4_bit_comparator_1_eq, _4_bit_comparator_2_eq);
endmodule
