// Digital circuit 8-bit-register.dig as structural Verilog
module _8_bit_register (
  input  CLR,
  input  CLK,
  input  EN,
  input  [7:0] D,
  output [7:0] Q
);

  // D_Flip_Flop d_flip_flop_1: pin names not known; wires that end beside it: D[0], CLK, CLR, EN, Q[0]
  // D_Flip_Flop d_flip_flop_2: pin names not known; wires that end beside it: D[1], CLK, CLR, EN, Q[1]
  // D_Flip_Flop d_flip_flop_3: pin names not known; wires that end beside it: D[2], CLK, CLR, EN, Q[2]
  // D_Flip_Flop d_flip_flop_4: pin names not known; wires that end beside it: D[3], CLK, CLR, EN, Q[3]
  // D_Flip_Flop d_flip_flop_5: pin names not known; wires that end beside it: D[4], CLK, CLR, EN, Q[4]
  // D_Flip_Flop d_flip_flop_6: pin names not known; wires that end beside it: D[5], CLK, CLR, EN, Q[5]
  // D_Flip_Flop d_flip_flop_7: pin names not known; wires that end beside it: D[6], CLK, CLR, EN, Q[6]
  // D_Flip_Flop d_flip_flop_8: pin names not known; wires that end beside it: D[7], CLK, CLR, EN, Q[7]
endmodule
