// Digital circuit ALU op.dig as structural Verilog
module ALU_op (
  input  [63:0] A,
  input  [63:0] B,
  input  [2:0] ALUOP,
  output [63:0] R
);

  wire [63:0] add_1_s, and_1_out, mul_1_mul, or_1_out, SLL_out, SRA_out, SRL_out, sub_1_s;

  Add #(.Bits(64)) add_1 (.a(A), .b(B), .c_i(1'b0), .s(add_1_s));  // open: c_o
  Sub #(.Bits(64)) sub_1 (.a(A), .b(B), .c_i(1'b0), .s(sub_1_s));  // open: c_o
  assign or_1_out = A | B;  // Or or_1, 64 bits wide
  Mul #(.Bits(32)) mul_1 (.a(A[31:0]), .b(B[31:0]), .mul(mul_1_mul));
  BarrelShifter #(.Bits(64)) SLL (.in(A), .shift(B[6:0]), .out(SLL_out));
  assign and_1_out = A & B;  // And and_1, 64 bits wide
  BarrelShifter #(.Bits(64), .direction("right")) SRL (.in(A), .shift(B[6:0]), .out(SRL_out));
  BarrelShifter #(.Bits(64), .barrelShifterMode("arithmetic"), .direction("right")) SRA (
    .in(A), .shift(B[6:0]), .out(SRA_out));
  Multiplexer #(.Selector_Bits(3), .Bits(64)) multiplexer_1 (
    .sel(ALUOP), .in_0(add_1_s), .in_1(sub_1_s), .in_2(or_1_out), .in_3(mul_1_mul), .in_4(SLL_out),
    .in_5(and_1_out), .in_6(SRL_out), .in_7(SRA_out), .out(R));
endmodule
