// Digital circuit BuOP.dig as structural Verilog
module BuOP (
  input  [1:0] BraOP,
  input  [63:0] RD0,
  input  [63:0] RD1,
  output Output
);

  wire BEQ_eq, BGE_eq, BGE_gt, BLT_lt, not_1_out, or_1_out;

  Comparator #(.Bits(64)) BEQ (.a(RD0), .b(RD1), .eq(BEQ_eq));  // open: gt, lt
  Comparator #(.Bits(64)) BLT (.a(RD0), .b(RD1), .lt(BLT_lt));  // open: gt, eq
  Comparator #(.Bits(64)) BGE (.a(RD0), .b(RD1), .gt(BGE_gt), .eq(BGE_eq));  // open: lt
  or or_1 (or_1_out, BGE_gt, BGE_eq);
  Multiplexer #(.Selector_Bits(2)) multiplexer_1 (
    .sel(BraOP), .in_0(BEQ_eq), .in_1(not_1_out), .in_2(BLT_lt), .in_3(or_1_out), .out(Output));
  not not_1 (not_1_out, BEQ_eq);
endmodule
