// Digital circuit Enable Decoder.dig as structural Verilog
module Enable_Decoder (
  input  [4:0] Sel,
  input  WE_EN,
  output r0,
  output r1,
  output r2,
  output r3,
  output r4,
  output r5,
  output r6,
  output r7,
  output r8,
  output r9,
  output r10,
  output r11,
  output r12,
  output r13,
  output r14,
  output r15,
  output r16,
  output r17,
  output r18,
  output r19,
  output r20,
  output r21,
  output r22,
  output r23,
  output r24,
  output r25,
  output r26,
  output r27,
  output r28,
  output r29,
  output r30,
  output r31
);

  wire decoder_1_out_0, decoder_1_out_1, decoder_1_out_2, decoder_1_out_3, decoder_1_out_4, decoder_1_out_5,
       decoder_1_out_6, decoder_1_out_7, decoder_1_out_8, decoder_1_out_9, decoder_1_out_10,
       decoder_1_out_11, decoder_1_out_12, decoder_1_out_13, decoder_1_out_14, decoder_1_out_15,
       decoder_1_out_16, decoder_1_out_17, decoder_1_out_18, decoder_1_out_19, decoder_1_out_20,
       decoder_1_out_21, decoder_1_out_22, decoder_1_out_23, decoder_1_out_24, decoder_1_out_25,
       decoder_1_out_26, decoder_1_out_27, decoder_1_out_28, decoder_1_out_29, decoder_1_out_30,
       decoder_1_out_31;

  Decoder #(.Selector_Bits(5)) decoder_1 (
    .sel(Sel), .out_0(decoder_1_out_0), .out_1(decoder_1_out_1), .out_2(decoder_1_out_2),
    .out_3(decoder_1_out_3), .out_4(decoder_1_out_4), .out_5(decoder_1_out_5), .out_6(decoder_1_out_6),
    .out_7(decoder_1_out_7), .out_8(decoder_1_out_8), .out_9(decoder_1_out_9), .out_10(decoder_1_out_10),
    .out_11(decoder_1_out_11), .out_12(decoder_1_out_12), .out_13(decoder_1_out_13),
    .out_14(decoder_1_out_14), .out_15(decoder_1_out_15), .out_16(decoder_1_out_16),
    .out_17(decoder_1_out_17), .out_18(decoder_1_out_18), .out_19(decoder_1_out_19),
    .out_20(decoder_1_out_20), .out_21(decoder_1_out_21), .out_22(decoder_1_out_22),
    .out_23(decoder_1_out_23), .out_24(decoder_1_out_24), .out_25(decoder_1_out_25),
    .out_26(decoder_1_out_26), .out_27(decoder_1_out_27), .out_28(decoder_1_out_28),
    .out_29(decoder_1_out_29), .out_30(decoder_1_out_30), .out_31(decoder_1_out_31));
  and and_1 (r0, decoder_1_out_0, WE_EN);
  and and_2 (r1, decoder_1_out_1, WE_EN);
  and and_3 (r2, decoder_1_out_2, WE_EN);
  and and_4 (r3, decoder_1_out_3, WE_EN);
  and and_5 (r4, decoder_1_out_4, WE_EN);
  and and_6 (r5, decoder_1_out_5, WE_EN);
  and and_7 (r6, decoder_1_out_6, WE_EN);
  and and_8 (r7, decoder_1_out_7, WE_EN);
  and and_9 (r8, decoder_1_out_8, WE_EN);
  and and_10 (r9, decoder_1_out_9, WE_EN);
  and and_11 (r10, decoder_1_out_10, WE_EN);
  and and_12 (r11, decoder_1_out_11, WE_EN);
  and and_13 (r12, decoder_1_out_12, WE_EN);
  and and_14 (r13, decoder_1_out_13, WE_EN);
  and and_15 (r14, decoder_1_out_14, WE_EN);
  and and_16 (r15, decoder_1_out_15, WE_EN);
  and and_17 (r16, decoder_1_out_16, WE_EN);
  and and_18 (r17, decoder_1_out_17, WE_EN);
  and and_19 (r18, decoder_1_out_18, WE_EN);
  and and_20 (r19, decoder_1_out_19, WE_EN);
  and and_21 (r20, decoder_1_out_20, WE_EN);
  and and_22 (r21, decoder_1_out_21, WE_EN);
  and and_23 (r22, decoder_1_out_22, WE_EN);
  and and_24 (r23, decoder_1_out_23, WE_EN);
  and and_25 (r24, decoder_1_out_24, WE_EN);
  and and_26 (r25, decoder_1_out_25, WE_EN);
  and and_27 (r26, decoder_1_out_26, WE_EN);
  and and_28 (r27, decoder_1_out_27, WE_EN);
  and and_29 (r28, decoder_1_out_28, WE_EN);
  and and_30 (r29, decoder_1_out_29, WE_EN);
  and and_31 (r30, decoder_1_out_30, WE_EN);
  and and_32 (r31, decoder_1_out_31, WE_EN);
endmodule
