// Digital circuit ImmDecoder.dig as structural Verilog
module ImmDecoder (
  input  [31:0] IW,
  output [63:0] imm_B,
  output [63:0] imm_U,
  output [63:0] imm_I,
  output [63:0] imm_S,
  output [63:0] imm_J,
  output [63:0] imm_I_64
);

  BitExtender #(.inputBits(20), .outputBits(64)) bitextender_1 (.in(IW[31:12]), .out(imm_U));
  BitExtender #(.inputBits(12), .outputBits(64)) bitextender_2 (.in(IW[31:20]), .out(imm_I));
  BitExtender #(.inputBits(21), .outputBits(64)) bitextender_3 (
    .in({IW[31], IW[19:12], IW[20], IW[30:21], 1'b0}), .out(imm_J));
  BitExtender #(.inputBits(12), .outputBits(64)) bitextender_4 (.in({IW[31:25], IW[11:7]}), .out(imm_S));
  BitExtender #(.inputBits(12), .outputBits(64)) bitextender_5 (.in({IW[31:25], IW[11:7]}), .out(imm_B));

  assign imm_I_64 = {{58{1'b0}}, IW[25:20]};
endmodule
