// Digital circuit Instructions.dig as structural Verilog
module Instructions (
  input  [4:0] INUM,
  input  Counter,
  output [7:0] c1,
  output [7:0] c2,
  output [7:0] c3,
  output [7:0] c4,
  output [63:0] Instruction
);

  wire [63:0] add_1_s, register_1_q;

  // Probe on INUM
  Register #(.Bits(64), .isProgramCounter("true")) register_1 (.D(add_1_s), .C(Counter), .en(1'b1), .Q(register_1_q));
  ROM #(.AddrBits(5), .Bits(32)) Rom (.A(INUM), .sel(1'b1), .D({c1, c2, c3, c4}));
  Add #(.Bits(64)) add_1 (.a(register_1_q), .b(64'h1), .c_i(1'b0), .s(add_1_s));  // open: c_o
  // Probe on {c1, c2, c3, c4}
  Sub #(.Bits(64)) sub_1 (.a(add_1_s), .b(64'h1), .c_i(1'b0), .s(Instruction));  // open: c_o

  // Notes on the sheet:
  //   contents of Rom (hex, n*v repeats v):
  //   41444449,41444452,4a414c,4a414c52,535542,4d554c,534c4c,534c4c49
  //   ,53524c,53524c49,42455100,424c5400,42474500,424e4500,4c440000
  //   ,53440000,4c570000,53570000,4c420000,4c425500,4f520000,4c490000
endmodule
