// Digital circuit load.dig as structural Verilog
module load (
  input  [63:0] TA,
  input  [1:0] MSZ,
  input  [63:0] DOUT,
  output [63:0] OUT
);

  wire [7:0] multiplexer_2_out;
  wire [31:0] multiplexer_1_out;
  wire [63:0] bitextender_1_out, bitextender_2_out;

  Multiplexer #(.Bits(32)) multiplexer_1 (.sel(TA[2]), .in_0(DOUT[31:0]), .in_1(DOUT[63:32]), .out(multiplexer_1_out));
  BitExtender #(.inputBits(32), .outputBits(64)) bitextender_1 (.in(multiplexer_1_out), .out(bitextender_1_out));
  Multiplexer #(.Selector_Bits(3), .Bits(8)) multiplexer_2 (
    .sel(TA[2:0]), .in_0(DOUT[7:0]), .in_1(DOUT[15:8]), .in_2(DOUT[23:16]), .in_3(DOUT[31:24]),
    .in_4(DOUT[39:32]), .in_5(DOUT[47:40]), .in_6(DOUT[55:48]), .in_7(DOUT[63:56]), .out(multiplexer_2_out));
  BitExtender #(.outputBits(64)) bitextender_2 (.in(multiplexer_2_out), .out(bitextender_2_out));
  Multiplexer #(.Selector_Bits(2), .Bits(64)) multiplexer_3 (
    .sel(MSZ), .in_0(DOUT), .in_1(bitextender_1_out), .in_2(bitextender_2_out), .in_3({64{1'b0}}), .out(OUT));
endmodule
