// Digital circuit project06-Part2-Branch.dig as structural Verilog
module project06_Part2_Branch (
  input  CLK,
  input  EN,
  input  CLR,
  input  [4:0] PROG,
  output DONE,
  output [63:0] zero,
  output [63:0] ra,
  output [63:0] sp,
  output [63:0] gp,
  output [63:0] tp,
  output [63:0] t0,
  output [63:0] t1,
  output [63:0] t2,
  output [63:0] s0_fp,
  output [63:0] s1,
  output [63:0] A0,
  output [63:0] A1,
  output [63:0] A2,
  output [63:0] A3,
  output [63:0] a4,
  output [63:0] a5,
  output [63:0] a6,
  output [63:0] a7,
  output [63:0] s2,
  output [63:0] s3,
  output [63:0] s4,
  output [63:0] s5,
  output [63:0] s6,
  output [63:0] s7,
  output [63:0] s8,
  output [63:0] s9,
  output [63:0] s10,
  output [63:0] s11,
  output [63:0] t3,
  output [63:0] t4,
  output [63:0] t5,
  output [63:0] t6
);

  wire _2reasonswhy_1_p10, ALUSrcA, and_2_out, CLK_t, instructions_1_p2, instructions_1_p3,
       instructions_1_p4, instructions_1_p5, PCbr, RFW, WDsel;
  wire [1:0] _2reasonswhy_1_p11, PCsel;
  wire [2:0] ALUOp, ALUSrcB;
  wire [4:0] rd, rs1, rs2;
  wire [31:0] iw;
  wire [63:0] alu_op_1_r, imm_I, immdecoder_1_imm_s, immdecoder_1_imm_u, multiplexer_1_out,
       multiplexer_2_out, multiplexer_3_out, multiplexer_4_out, multiplexer_5_out, PC, PC_plus_4_s,
       register_file_rd0, register_file_rd1;

  Multiplexer #(.Bits(64)) multiplexer_1 (.sel(PCbr), .in_0(alu_op_1_r), .in_1(PC_plus_4_s), .out(multiplexer_1_out));
  Multiplexer #(.Selector_Bits(2), .Bits(64)) multiplexer_2 (
    .sel(PCsel), .in_0(PC_plus_4_s), .in_1(alu_op_1_r), .in_2(multiplexer_1_out), .in_3({64{1'b0}}),
    .out(multiplexer_2_out));
  // Probe on PC
  // Probe on iw
  // Probe on rs1
  // Probe on rs2
  // Probe on rd
  // Probe on imm_I
  // Probe on iw
  Comparator #(.Bits(32)) End (.a(iw), .b(32'hc0001073), .eq(DONE));  // open: gt, lt
  Clear_register clear_register_1 (.D(multiplexer_2_out), .CLK(CLK_t), .EN(EN), .CLR(CLR), .Q(PC));
  and and_1 (CLK_t, CLK, ~DONE);  // And
  LED led_1 (.in(DONE));
  // inst_mem inst_mem_1: pin names not known; wires that end beside it: PROG, PC[10:2], iw
  Add #(.Bits(64)) PC_plus_4 (.a(PC), .b(64'h4), .c_i(1'b0), .s(PC_plus_4_s));  // open: c_o
  RegDecoder regdecoder_1 (.IW(iw), .RS2(rs2), .RS1(rs1), .RD(rd));
  // _2reasonswhy _2reasonswhy_1: pin names not known; wires that end beside it: iw[6:0], iw[14:12], iw[31:25], RFW, PCsel, WDsel, ALUSrcB, ALUOp, ALUSrcA, _2reasonswhy_1_p10, _2reasonswhy_1_p11
  // Instructions instructions_1: pin names not known; wires that end beside it: _2reasonswhy_1_p10, instructions_1_p2, instructions_1_p3, instructions_1_p4, instructions_1_p5
  // Probe on _2reasonswhy_1_p10
  Multiplexer #(.Bits(64)) multiplexer_3 (.sel(WDsel), .in_0(alu_op_1_r), .in_1(PC_plus_4_s), .out(multiplexer_3_out));
  // Probe on instructions_1_p2
  and and_2 (and_2_out, RFW, EN);
  ImmDecoder immdecoder_1 (
    .IW(iw), .imm_U(immdecoder_1_imm_u), .imm_S(immdecoder_1_imm_s), .imm_J(imm_I));  // open: imm_B, imm_I, imm_I_64
  // Probe on instructions_1_p3
  // Probe on instructions_1_p4
  // Probe on instructions_1_p5
  register_file register_file (
    .RR0(rs1), .RR1(rs2), .WR(rd), .WEN(and_2_out), .CLR(CLR), .CLK(CLK_t), .Write_Data(multiplexer_3_out),
    .RD0(register_file_rd0), .RD1(register_file_rd1), .x0(zero), .x1(ra), .x2(sp), .x3(gp), .x4(tp), .x5(t0),
    .x6(t1), .x7(t2), .x8(s0_fp), .x9(s1), .x10(A0), .x11(A1), .x12(A2), .x13(A3), .x14(a4), .x15(a5),
    .x16(a6), .x17(a7), .x18(s2), .x19(s3), .x20(s4), .x21(s5), .x22(s6), .x23(s7), .x24(s8), .x25(s9),
    .x26(s10), .x27(s11), .x28(t3), .x29(t4), .x30(t5), .x31(t6));
  Multiplexer #(.Bits(64)) multiplexer_4 (.sel(ALUSrcA), .in_0(register_file_rd0), .in_1(PC), .out(multiplexer_4_out));
  BuOP buop_1 (.BraOP(_2reasonswhy_1_p11), .RD0(register_file_rd0), .RD1(register_file_rd1), .Output(PCbr));
  Multiplexer #(.Selector_Bits(3), .Bits(64)) multiplexer_5 (
    .sel(ALUSrcB), .in_0(register_file_rd1), .in_1(imm_I), .in_2(immdecoder_1_imm_s),
    .in_3(immdecoder_1_imm_u), .in_4({64{1'b0}}), .in_5({64{1'b0}}), .in_6({64{1'b0}}), .in_7({64{1'b0}}),
    .out(multiplexer_5_out));
  // Probe on ALUSrcB
  // Probe on PCbr
  ALU_op alu_op_1 (.A(multiplexer_4_out), .B(multiplexer_5_out), .ALUOP(ALUOp), .R(alu_op_1_r));

  // Other names for the same wires on the sheet: x0[63:0] = zero; x1[63:0] = ra; x2[63:0] = sp; x3[63:0] = gp;
  //   x4[63:0] = tp; x5[63:0] = t0; x6[63:0] = t1; x7[63:0] = t2; x8[63:0] = s0_fp; x9[63:0] = s1; x10[63:0] = A0;
  //   x11[63:0] = A1; x12[63:0] = A2; x13[63:0] = A3; x14[63:0] = a4; x15[63:0] = a5; x16[63:0] = a6; x17[63:0] = a7;
  //   x18[63:0] = s2; x19[63:0] = s3; x20[63:0] = s4; x21[63:0] = s5; x22[63:0] = s6; x23[63:0] = s7; x24[63:0] = s8;
  //   x25[63:0] = s9; x26[63:0] = s10; x27[63:0] = s11; x28[63:0] = t3; x29[63:0] = t4; x30[63:0] = t5;
  //   x31[63:0] = t6
endmodule

/* Test case:
CLR EN CLK PROG A0 A1 A2 A3
1   0   0   x    x    x    x    x
0   0   0   x    x    x    x    x
while (!(DONE))
0   1   C   10    x    x    x    x
end while
0   1   0   10 1  2  0  0
*/
