// Digital circuit project06-Part4-Load.dig as structural Verilog
module project06_Part4_Load (
  input  [4:0] PROG,
  input  CLK,
  input  CLR,
  input  EN,
  output [63:0] A0,
  output [63:0] A1,
  output [63:0] A2,
  output DONE,
  output [63:0] A3
);

  wire ALUSrcA, and_2_out, CLK_t, instructions_1_p2, instructions_1_p3, instructions_1_p4, instructions_1_p5,
       MLD, MST, PCbr, RFW;
  wire [1:0] BRAOp, MSZ, PCsel, WDsel;
  wire [2:0] ALUOp, ALUSrcB;
  wire [4:0] instructions_1_p1, rd, rs1, rs2;
  wire [31:0] iw;
  wire [63:0] add_1_s, alu_op_1_r, imm_I, immdecoder_1_imm_b, immdecoder_1_imm_j, immdecoder_1_imm_s,
       load_1_out, multiplexer_1_out, multiplexer_2_out, multiplexer_3_out, multiplexer_4_out,
       multiplexer_5_out, PC, ramdualport_1_d, register_file_1_rd0, register_file_1_rd1, store_1_dwn, x0, x1,
       x2, x3, x4, x5, x6, x7, x8, x9, x14, x15, x16, x17, x18, x19, x20, x21, x22, x23, x24, x25, x26, x27,
       x28, x29, x30, x31;

  Multiplexer #(.Selector_Bits(2), .Bits(64)) multiplexer_1 (
    .sel(PCsel), .in_0(add_1_s), .in_1(alu_op_1_r), .in_2(multiplexer_2_out), .in_3({64{1'b0}}),
    .out(multiplexer_1_out));
  Multiplexer #(.Bits(64)) multiplexer_2 (.sel(PCbr), .in_0(add_1_s), .in_1(alu_op_1_r), .out(multiplexer_2_out));
  Clear_register clear_register_1 (.D(multiplexer_1_out), .CLK(CLK_t), .EN(EN), .CLR(CLR), .Q(PC));
  Comparator #(.Bits(32)) comparator_1 (.a(iw), .b(32'hc0001073), .eq(DONE));  // open: gt, lt
  and and_1 (CLK_t, CLK, ~DONE);  // And
  LED led_1 (.in(DONE));
  Add #(.Bits(64)) add_1 (.a(PC), .b(64'h4), .c_i(1'b0), .s(add_1_s));  // open: c_o
  // Probe on instructions_1_p1
  // inst_mem inst_mem_1: pin names not known; wires that end beside it: PROG, PC[10:2], iw
  // Instructions instructions_1: pin names not known; wires that end beside it: instructions_1_p1, instructions_1_p2, instructions_1_p3, instructions_1_p4, instructions_1_p5
  // Probe on instructions_1_p2
  // Probe on instructions_1_p3
  // Probe on iw
  // Probe on instructions_1_p4
  // Probe on instructions_1_p5
  RegDecoder regdecoder_1 (.IW(iw), .RS2(rs1), .RS1(rs2), .RD(rd));
  _2reasonswhy _2reasonswhy_1 (
    .opcode(iw[6:0]), .funct3(iw[14:12]), .funct7(iw[31:25]), .RFW(RFW), .PCsel(PCsel), .WDsel(WDsel),
    .ALUSrcB(ALUSrcB), .ALUOP(ALUOp), .ALUSrcA(ALUSrcA), .INUM(instructions_1_p1), .BRAOP(BRAOp), .MLD(MLD),
    .MST(MST), .MZD(MSZ));
  ImmDecoder immdecoder_1 (
    .IW(iw), .imm_B(immdecoder_1_imm_b), .imm_I(imm_I), .imm_S(immdecoder_1_imm_s), .imm_J(immdecoder_1_imm_j));  // open: imm_U, imm_I_64
  // Probe on rs1
  // Probe on rs1
  and and_2 (and_2_out, RFW, EN);
  // Probe on WDsel
  Multiplexer #(.Selector_Bits(2), .Bits(64)) multiplexer_3 (
    .sel(WDsel), .in_0(alu_op_1_r), .in_1(add_1_s), .in_2(load_1_out), .in_3({64{1'b0}}),
    .out(multiplexer_3_out));
  // Probe on rs2
  // Probe on rd
  // Probe on multiplexer_3_out
  // Probe on multiplexer_3_out
  register_file register_file_1 (
    .RR0(rs2), .RR1(rs1), .WR(rd), .WEN(and_2_out), .CLR(CLR), .CLK(CLK_t), .Write_Data(multiplexer_3_out),
    .RD0(register_file_1_rd0), .RD1(register_file_1_rd1), .x0(x0), .x1(x1), .x2(x2), .x3(x3), .x4(x4),
    .x5(x5), .x6(x6), .x7(x7), .x8(x8), .x9(x9), .x10(A0), .x11(A1), .x12(A2), .x13(A3), .x14(x14),
    .x15(x15), .x16(x16), .x17(x17), .x18(x18), .x19(x19), .x20(x20), .x21(x21), .x22(x22), .x23(x23),
    .x24(x24), .x25(x25), .x26(x26), .x27(x27), .x28(x28), .x29(x29), .x30(x30), .x31(x31));
  BuOP buop_1 (.BraOP(BRAOp), .RD0(register_file_1_rd0), .RD1(register_file_1_rd1), .Output(PCbr));
  Multiplexer #(.Bits(64)) multiplexer_4 (
    .sel(ALUSrcA), .in_0(register_file_1_rd0), .in_1(PC), .out(multiplexer_4_out));
  // Probe on ALUSrcB
  Multiplexer #(.Selector_Bits(3), .Bits(64)) multiplexer_5 (
    .sel(ALUSrcB), .in_0(register_file_1_rd1), .in_1(imm_I), .in_2(immdecoder_1_imm_j),
    .in_3(immdecoder_1_imm_b), .in_4(immdecoder_1_imm_s), .in_5({64{1'b0}}), .in_6({64{1'b0}}),
    .in_7({64{1'b0}}), .out(multiplexer_5_out));
  ALU_op alu_op_1 (.A(multiplexer_4_out), .B(multiplexer_5_out), .ALUOP(ALUOp), .R(alu_op_1_r));
  store store_1 (.TA(alu_op_1_r), .MSZ(MSZ), .RD1(register_file_1_rd1), .DOUT(ramdualport_1_d), .dwn(store_1_dwn));
  RAMDualPort #(.AddrBits(7), .Bits(64)) ramdualport_1 (
    .A(alu_op_1_r[9:3]), .Din(store_1_dwn), .str(MST), .C(CLK_t), .ld(MLD), .D(ramdualport_1_d));
  load load_1 (.MSZ(MSZ), .TA(alu_op_1_r), .DOUT(ramdualport_1_d), .OUT(load_1_out));
  // Probe on ramdualport_1_d
  // Probe on load_1_out

  // Other names for the same wires on the sheet: x10[63:0] = A0; x11[63:0] = A1; x12[63:0] = A2; x13[63:0] = A3
endmodule

/* Test case:
CLR EN CLK PROG A0 A1 A2 A3
1   0   0   x    x    x    x    x
0   0   0   x    x    x    x    x
while (!(DONE))
0   1   C   13    x    x    x    x
end while
0   1   0   13 99  0  0  0
*/

/* Test case addi:
CLR EN CLK PROG A0 A1 A2 A3
1   0   0   x    x    x    x    x
0   0   0   x    x    x    x    x
while (!(DONE))
0   1   C   0    x    x    x    x
end while
0   1   0   0 3  0  0  0
*/
