// Digital circuit project06.dig as structural Verilog
module project06 (
  input  [4:0] PROG,
  input  CLK,
  input  CLR,
  input  EN,
  output [63:0] A0,
  output [63:0] A1,
  output [63:0] A2,
  output DONE,
  output [63:0] A3,
  output DONE_2,
  output [63:0] zero,
  output [63:0] ra,
  output [63:0] sp,
  output [63:0] gp,
  output [63:0] tp,
  output [63:0] t0,
  output [63:0] t1,
  output [63:0] t2,
  output [63:0] s0_fp,
  output [63:0] s1,
  output [63:0] A4,
  output [63:0] A5,
  output [63:0] A6,
  output [63:0] A7,
  output [63:0] a4_2,
  output [63:0] a5_2,
  output [63:0] a6_2,
  output [63:0] a7_2,
  output [63:0] s2,
  output [63:0] s3,
  output [63:0] s4,
  output [63:0] s5,
  output [63:0] s6,
  output [63:0] s7,
  output [63:0] s8,
  output [63:0] s9,
  output [63:0] s10,
  output [63:0] s11,
  output [63:0] t3,
  output [63:0] t4,
  output [63:0] t5,
  output [63:0] t6
);

  wire ALUSrcA, and_1_out, and_3_out, CLK_t, MLD, MST, PCbr, RFW;
  wire [1:0] BRAOp, MSZ, PCsel, WDsel;
  wire [2:0] ALUOp, ALUSrcB;
  wire [4:0] _2reasonswhy_1_inum, rd, rs1, rs2;
  wire [7:0] instructions_1_c1, instructions_1_c2, instructions_1_c3, instructions_1_c4;
  wire [31:0] iw;
  wire [63:0] add_1_s, alu_op_1_r, imm_I, immdecoder_1_imm_b, immdecoder_1_imm_i_64, immdecoder_1_imm_j,
       immdecoder_1_imm_s, instructions_1_instruction, load_1_out, multiplexer_1_out, multiplexer_2_out,
       multiplexer_3_out, multiplexer_4_out, multiplexer_5_out, PC, ramdualport_1_d, register_file_1_rd0,
       register_file_1_rd1, store_1_dwn;

  Multiplexer #(.Selector_Bits(2), .Bits(64)) multiplexer_1 (
    .sel(PCsel), .in_0(add_1_s), .in_1(alu_op_1_r), .in_2(multiplexer_2_out), .in_3({64{1'b0}}),
    .out(multiplexer_1_out));
  Multiplexer #(.Bits(64)) multiplexer_2 (.sel(PCbr), .in_0(add_1_s), .in_1(alu_op_1_r), .out(multiplexer_2_out));
  and and_1 (and_1_out, CLK_t, EN);
  Instructions instructions_1 (
    .INUM(_2reasonswhy_1_inum), .Counter(and_1_out), .c1(instructions_1_c1), .c2(instructions_1_c2),
    .c3(instructions_1_c3), .c4(instructions_1_c4), .Instruction(instructions_1_instruction));
  Clear_register clear_register_1 (.D(multiplexer_1_out), .CLK(CLK_t), .EN(EN), .CLR(CLR), .Q(PC));
  and and_2 (CLK_t, CLK, ~DONE);  // And
  Comparator #(.Bits(32)) comparator_1 (.a(iw), .b(32'hc0001073), .eq(DONE));  // open: gt, lt
  // Probe on instructions_1_c1
  // Probe on instructions_1_c2
  LED led_1 (.in(DONE));
  Add #(.Bits(64)) add_1 (.a(PC), .b(64'h4), .c_i(1'b0), .s(add_1_s));  // open: c_o
  // Probe on instructions_1_c3
  // Probe on instructions_1_c4
  // Probe on instructions_1_instruction
  // inst_mem inst_mem_1: pin names not known; wires that end beside it: PROG, PC[10:2], iw
  // Probe on iw
  // Probe on ALUSrcA
  // Probe on ALUSrcB
  // Probe on ALUOp
  // Probe on MSZ
  RegDecoder regdecoder_1 (.IW(iw), .RS2(rs1), .RS1(rs2), .RD(rd));
  _2reasonswhy _2reasonswhy_1 (
    .opcode(iw[6:0]), .funct3(iw[14:12]), .funct7(iw[31:25]), .RFW(RFW), .PCsel(PCsel), .WDsel(WDsel),
    .ALUSrcB(ALUSrcB), .ALUOP(ALUOp), .ALUSrcA(ALUSrcA), .INUM(_2reasonswhy_1_inum), .BRAOP(BRAOp),
    .MLD(MLD), .MST(MST), .MZD(MSZ));
  and and_3 (and_3_out, RFW, EN);
  // Probe on WDsel
  Multiplexer #(.Selector_Bits(2), .Bits(64)) multiplexer_3 (
    .sel(WDsel), .in_0(alu_op_1_r), .in_1(add_1_s), .in_2(load_1_out), .in_3({64{1'b0}}),
    .out(multiplexer_3_out));
  ImmDecoder immdecoder_1 (
    .IW(iw), .imm_B(immdecoder_1_imm_b), .imm_I(imm_I), .imm_S(immdecoder_1_imm_s),
    .imm_J(immdecoder_1_imm_j), .imm_I_64(immdecoder_1_imm_i_64));  // open: imm_U
  // Probe on multiplexer_3_out
  // Probe on multiplexer_3_out
  register_file register_file_1 (
    .RR0(rs2), .RR1(rs1), .WR(rd), .WEN(and_3_out), .CLR(CLR), .CLK(CLK_t), .Write_Data(multiplexer_3_out),
    .RD0(register_file_1_rd0), .RD1(register_file_1_rd1), .x0(zero), .x1(ra), .x2(sp), .x3(gp), .x4(tp),
    .x5(t0), .x6(t1), .x7(t2), .x8(s0_fp), .x9(s1), .x10(A0), .x11(A1), .x12(A2), .x13(A3), .x14(a4_2),
    .x15(a5_2), .x16(a6_2), .x17(a7_2), .x18(s2), .x19(s3), .x20(s4), .x21(s5), .x22(s6), .x23(s7), .x24(s8),
    .x25(s9), .x26(s10), .x27(s11), .x28(t3), .x29(t4), .x30(t5), .x31(t6));
  BuOP buop_1 (.BraOP(BRAOp), .RD0(register_file_1_rd0), .RD1(register_file_1_rd1), .Output(PCbr));
  Multiplexer #(.Bits(64)) multiplexer_4 (
    .sel(ALUSrcA), .in_0(register_file_1_rd0), .in_1(PC), .out(multiplexer_4_out));
  // Probe on ALUSrcB
  Multiplexer #(.Selector_Bits(3), .Bits(64)) multiplexer_5 (
    .sel(ALUSrcB), .in_0(register_file_1_rd1), .in_1(imm_I), .in_2(immdecoder_1_imm_j),
    .in_3(immdecoder_1_imm_b), .in_4(immdecoder_1_imm_s), .in_5(immdecoder_1_imm_i_64), .in_6({64{1'b0}}),
    .in_7({64{1'b0}}), .out(multiplexer_5_out));
  ALU_op alu_op_1 (.A(multiplexer_4_out), .B(multiplexer_5_out), .ALUOP(ALUOp), .R(alu_op_1_r));
  store store_1 (.TA(alu_op_1_r), .MSZ(MSZ), .RD1(register_file_1_rd1), .DOUT(ramdualport_1_d), .dwn(store_1_dwn));
  RAMDualPort #(.AddrBits(7), .Bits(64)) ramdualport_1 (
    .A(alu_op_1_r[9:3]), .Din(store_1_dwn), .str(MST), .C(CLK_t), .ld(MLD), .D(ramdualport_1_d));
  load load_1 (.MSZ(MSZ), .TA(alu_op_1_r), .DOUT(ramdualport_1_d), .OUT(load_1_out));

  assign A4 = A0;
  assign A5 = A1;
  assign A6 = A2;
  assign A7 = A3;
  assign DONE_2 = DONE;

  // Other names for the same wires on the sheet: x0[63:0] = zero; x1[63:0] = ra; x2[63:0] = sp; x3[63:0] = gp;
  //   x4[63:0] = tp; x5[63:0] = t0; x6[63:0] = t1; x7[63:0] = t2; x8[63:0] = s0_fp; x9[63:0] = s1; x10[63:0] = A0;
  //   x11[63:0] = A1; x12[63:0] = A2; x13[63:0] = A3; x14[63:0] = a4_2; x15[63:0] = a5_2; x16[63:0] = a6_2;
  //   x17[63:0] = a7_2; x18[63:0] = s2; x19[63:0] = s3; x20[63:0] = s4; x21[63:0] = s5; x22[63:0] = s6;
  //   x23[63:0] = s7; x24[63:0] = s8; x25[63:0] = s9; x26[63:0] = s10; x27[63:0] = s11; x28[63:0] = t3;
  //   x29[63:0] = t4; x30[63:0] = t5; x31[63:0] = t6
endmodule

/* Test case 21-sort:
CLR EN CLK PROG A0 A1 A2 A3
1   0   0   x    x    x    x    x
0   0   0   x    x    x    x    x
while (!(DONE))
0   1   C   21    x    x    x    x
end while
0   1   0   21 8589934596  25769803784  42949672972  0
*/

/* Test case 19-toUpper:
CLR EN CLK PROG A0 A1 A2 A3
1   0   0   x    x    x    x    x
0   0   0   x    x    x    x    x
while (!(DONE))
0   1   C   19    x    x    x    x
end while
0   1   0   19 5066355251797426176  1014  0  0
*/

/* Test case 06-slli:
CLR EN CLK PROG A0 A1 A2 A3
1   0   0   x    x    x    x    x
0   0   0   x    x    x    x    x
while (!(DONE))
0   1   C   6    x    x    x    x
end while
0   1   0   6 8  1  0  0
*/
