// Digital circuit register_file.dig as structural Verilog
module register_file (
  input  [4:0] RR1,
  input  [4:0] RR0,
  input  [4:0] WR,
  input  WEN,
  input  [63:0] Write_Data,
  input  CLR,
  input  CLK,
  output [63:0] RD0,
  output [63:0] RD1,
  output [63:0] x0,
  output [63:0] x1,
  output [63:0] x2,
  output [63:0] x3,
  output [63:0] x4,
  output [63:0] x5,
  output [63:0] x6,
  output [63:0] x7,
  output [63:0] x8,
  output [63:0] x9,
  output [63:0] x10,
  output [63:0] x11,
  output [63:0] x12,
  output [63:0] x13,
  output [63:0] x14,
  output [63:0] x15,
  output [63:0] x16,
  output [63:0] x17,
  output [63:0] x18,
  output [63:0] x19,
  output [63:0] x20,
  output [63:0] x21,
  output [63:0] x22,
  output [63:0] x23,
  output [63:0] x24,
  output [63:0] x25,
  output [63:0] x26,
  output [63:0] x27,
  output [63:0] x28,
  output [63:0] x29,
  output [63:0] x30,
  output [63:0] x31
);

  wire EN0, EN1, EN2, EN3, EN4, EN5, EN6, EN7, EN8, EN9, EN10, EN11, EN12, EN13, EN14, EN15, EN16, EN17,
       EN18, EN19, EN20, EN21, EN22, EN23, EN24, EN25, EN26, EN27, EN28, EN29, EN30, EN31;

  Enable_Decoder enable_decoder_1 (
    .Sel(WR), .WE_EN(WEN), .r0(EN0), .r1(EN1), .r2(EN2), .r3(EN3), .r4(EN4), .r5(EN5), .r6(EN6), .r7(EN7),
    .r8(EN8), .r9(EN9), .r10(EN10), .r11(EN11), .r12(EN12), .r13(EN13), .r14(EN14), .r15(EN15), .r16(EN16),
    .r17(EN17), .r18(EN18), .r19(EN19), .r20(EN20), .r21(EN21), .r22(EN22), .r23(EN23), .r24(EN24),
    .r25(EN25), .r26(EN26), .r27(EN27), .r28(EN28), .r29(EN29), .r30(EN30), .r31(EN31));
  Clear_register clear_register_1 (.D(Write_Data), .CLK(CLK), .EN(EN0), .CLR(CLR), .Q(x0));
  Clear_register clear_register_2 (.D(Write_Data), .CLK(CLK), .EN(EN1), .CLR(CLR), .Q(x1));
  Clear_register clear_register_3 (.D(Write_Data), .CLK(CLK), .EN(EN2), .CLR(CLR), .Q(x2));
  Clear_register clear_register_4 (.D(Write_Data), .CLK(CLK), .EN(EN3), .CLR(CLR), .Q(x3));
  Clear_register clear_register_5 (.D(Write_Data), .CLK(CLK), .EN(EN4), .CLR(CLR), .Q(x4));
  Clear_register clear_register_6 (.D(Write_Data), .CLK(CLK), .EN(EN5), .CLR(CLR), .Q(x5));
  Clear_register clear_register_7 (.D(Write_Data), .CLK(CLK), .EN(EN6), .CLR(CLR), .Q(x6));
  Clear_register clear_register_8 (.D(Write_Data), .CLK(CLK), .EN(EN7), .CLR(CLR), .Q(x7));
  Clear_register u_EN8 (.D(Write_Data), .CLK(CLK), .EN(EN8), .CLR(CLR), .Q(x8));
  Clear_register clear_register_9 (.D(Write_Data), .CLK(CLK), .EN(EN9), .CLR(CLR), .Q(x9));
  Clear_register clear_register_10 (.D(Write_Data), .CLK(CLK), .EN(EN10), .CLR(CLR), .Q(x10));
  Clear_register clear_register_11 (.D(Write_Data), .CLK(CLK), .EN(EN11), .CLR(CLR), .Q(x11));
  Clear_register clear_register_12 (.D(Write_Data), .CLK(CLK), .EN(EN12), .CLR(CLR), .Q(x12));
  Clear_register clear_register_13 (.D(Write_Data), .CLK(CLK), .EN(EN13), .CLR(CLR), .Q(x13));
  Clear_register clear_register_14 (.D(Write_Data), .CLK(CLK), .EN(EN14), .CLR(CLR), .Q(x14));
  Clear_register clear_register_15 (.D(Write_Data), .CLK(CLK), .EN(EN15), .CLR(CLR), .Q(x15));
  Clear_register clear_register_16 (.D(Write_Data), .CLK(CLK), .EN(EN16), .CLR(CLR), .Q(x16));
  Clear_register u_EN17 (.D(Write_Data), .CLK(CLK), .EN(EN17), .CLR(CLR), .Q(x17));
  Clear_register clear_register_17 (.D(Write_Data), .CLK(CLK), .EN(EN18), .CLR(CLR), .Q(x18));
  Clear_register clear_register_18 (.D(Write_Data), .CLK(CLK), .EN(EN19), .CLR(CLR), .Q(x19));
  Clear_register clear_register_19 (.D(Write_Data), .CLK(CLK), .EN(EN20), .CLR(CLR), .Q(x20));
  Clear_register clear_register_20 (.D(Write_Data), .CLK(CLK), .EN(EN21), .CLR(CLR), .Q(x21));
  Clear_register clear_register_21 (.D(Write_Data), .CLK(CLK), .EN(EN22), .CLR(CLR), .Q(x22));
  Clear_register clear_register_22 (.D(Write_Data), .CLK(CLK), .EN(EN23), .CLR(CLR), .Q(x23));
  Clear_register clear_register_23 (.D(Write_Data), .CLK(CLK), .EN(EN24), .CLR(CLR), .Q(x24));
  Clear_register clear_register_24 (.D(Write_Data), .CLK(CLK), .EN(EN25), .CLR(CLR), .Q(x25));
  Clear_register clear_register_25 (.D(Write_Data), .CLK(CLK), .EN(EN26), .CLR(CLR), .Q(x26));
  Clear_register clear_register_26 (.D(Write_Data), .CLK(CLK), .EN(EN27), .CLR(CLR), .Q(x27));
  Clear_register clear_register_27 (.D(Write_Data), .CLK(CLK), .EN(EN28), .CLR(CLR), .Q(x28));
  Clear_register clear_register_28 (.D(Write_Data), .CLK(CLK), .EN(EN29), .CLR(CLR), .Q(x29));
  Clear_register clear_register_29 (.D(Write_Data), .CLK(CLK), .EN(EN30), .CLR(CLR), .Q(x30));
  Clear_register clear_register_30 (.D(Write_Data), .CLK(CLK), .EN(EN31), .CLR(CLR), .Q(x31));
  Multiplexer #(.Selector_Bits(5), .Bits(64)) multiplexer_1 (
    .sel(RR0), .in_0({64{1'b0}}), .in_1(x1), .in_2(x2), .in_3(x3), .in_4(x4), .in_5(x5), .in_6(x6),
    .in_7(x7), .in_8(x8), .in_9(x9), .in_10(x10), .in_11(x11), .in_12(x12), .in_13(x13), .in_14(x14),
    .in_15(x15), .in_16(x16), .in_17(x17), .in_18(x18), .in_19(x19), .in_20(x20), .in_21(x21), .in_22(x22),
    .in_23(x23), .in_24(x24), .in_25(x25), .in_26(x26), .in_27(x27), .in_28(x28), .in_29(x29), .in_30(x30),
    .in_31(x31), .out(RD0));
  Multiplexer #(.Selector_Bits(5), .Bits(64)) multiplexer_2 (
    .sel(RR1), .in_0({64{1'b0}}), .in_1(x1), .in_2(x2), .in_3(x3), .in_4(x4), .in_5(x5), .in_6(x6),
    .in_7(x7), .in_8(x8), .in_9(x9), .in_10(x10), .in_11(x11), .in_12(x12), .in_13(x13), .in_14(x14),
    .in_15(x15), .in_16(x16), .in_17(x17), .in_18(x18), .in_19(x19), .in_20(x20), .in_21(x21), .in_22(x22),
    .in_23(x23), .in_24(x24), .in_25(x25), .in_26(x26), .in_27(x27), .in_28(x28), .in_29(x29), .in_30(x30),
    .in_31(x31), .out(RD1));
endmodule
