// Digital circuit store.dig as structural Verilog
module store (
  input  [63:0] RD1,
  input  [63:0] TA,
  input  [63:0] DOUT,
  input  [1:0] MSZ,
  output [63:0] dwn
);

  wire [63:0] bwn, dwn_t;

  Multiplexer #(.Selector_Bits(2), .Bits(64)) multiplexer_1 (
    .sel(MSZ), .in_0(RD1), .in_1(dwn_t), .in_2(bwn), .in_3({64{1'b0}}), .out(dwn));
  Multiplexer #(.Bits(64)) multiplexer_2 (
    .sel(TA[2]), .in_0({DOUT[63:32], RD1[31:0]}), .in_1({RD1[31:0], DOUT[31:0]}), .out(dwn_t));
  Multiplexer #(.Selector_Bits(3), .Bits(64)) multiplexer_3 (
    .sel(TA[2:0]), .in_0({DOUT[63:8], RD1[7:0]}), .in_1({DOUT[63:16], RD1[7:0], DOUT[7:0]}),
    .in_2({DOUT[63:24], RD1[7:0], DOUT[15:0]}), .in_3({DOUT[63:32], RD1[7:0], DOUT[23:0]}),
    .in_4({DOUT[63:40], RD1[7:0], DOUT[31:0]}), .in_5({DOUT[63:48], RD1[7:0], DOUT[39:0]}),
    .in_6({DOUT[63:56], RD1[7:0], DOUT[47:0]}), .in_7({RD1[7:0], DOUT[55:0]}), .out(bwn));

  // Other names for the same wires on the sheet: b0[7:0] = DOUT[7:0]; w0[31:0] = DOUT[31:0]; b1[7:0] = DOUT[15:8];
  //   b2[7:0] = DOUT[23:16]; b3[7:0] = DOUT[31:24]; b4[7:0] = DOUT[39:32]; w1[31:0] = DOUT[63:32];
  //   b5[7:0] = DOUT[47:40]; b6[7:0] = DOUT[55:48]; b7[7:0] = DOUT[63:56]; bn[7:0] = RD1[7:0]; wn[31:0] = RD1[31:0]
endmodule
